// Logisim project 11_lib.circ as structural Verilog: 1 circuit, main circuit main
module main (
  input  in_1,
  input  in_2,
  input  in_3,
  input  in_4,
  input  in_5,
  input  in_6,
  input  in_7,
  input  in_8,
  input  in_9,
  input  in_10
);

  wire transistor_1_out, transistor_2_out, transistor_4_out, transistor_5_out, transistor_6_out,
       transistor_7_out, transistor_8_out, transistor_9_out;

  Transistor #(.\type ("n")) transistor_1 (.in(1'b1), .out(transistor_1_out), .gate(in_3));
  Transistor #(.\type ("n")) transistor_2 (.in(1'b1), .out(transistor_2_out), .gate(in_7));
  Transistor #(.\type ("n")) transistor_3 (.in(1'b1), .out(transistor_2_out), .gate(in_9));
  Transistor #(.\type ("n")) transistor_4 (.in(1'b1), .out(transistor_4_out), .gate(in_1));
  Transistor #(.\type ("n")) transistor_5 (.in(transistor_1_out), .out(transistor_5_out), .gate(in_4));
  LED led_1 (.in(transistor_4_out));
  LED led_2 (.in(transistor_5_out));
  LED led_3 (.in(transistor_2_out));
  Transistor transistor_6 (.in(1'b1), .out(transistor_6_out), .gate(in_2));
  LED led_4 (.in(transistor_6_out));
  Transistor transistor_7 (.in(1'b1), .out(transistor_7_out), .gate(in_5));
  Transistor transistor_8 (.in(transistor_7_out), .out(transistor_8_out), .gate(in_6));
  Transistor transistor_9 (.in(1'b1), .out(transistor_9_out), .gate(in_8));
  Transistor transistor_10 (.in(1'b1), .out(transistor_9_out), .gate(in_10));
  LED led_5 (.in(transistor_8_out));
  LED led_6 (.in(transistor_9_out));

  // Notes on the sheet:
  //   与门
  //   或门
  //   缓冲器N
  //   反向器P
  //   与非门
  //   或非门
endmodule
