// Logisim project 12_lib.circ as structural Verilog: 5 circuits, main circuit Xor Gate
module Xor_Gate (
  input  \输入A ,
  input  \输入B ,
  input  in_3,
  input  in_4,
  output \输出 ,
  output out_6
);

  wire nand_1_out, or_1_out;

  or or_1 (or_1_out, \输入A , \输入B );
  nand nand_1 (nand_1_out, \输入A , \输入B );
  xor xor_1 (out_6, in_3, in_4);
  and and_1 (\输出 , or_1_out, nand_1_out);

  // Notes on the sheet:
  //   异或门
endmodule

module Half_Adder (
  input  \输入A ,
  input  \输入B ,
  input  in_3,
  input  in_4,
  output \加和输出 ,
  output \进位输出 ,
  output out_7,
  output out_8
);

  Adder #(.width(1)) adder_1 (.a(in_3), .b(in_4), .out(out_7), .cout(out_8));  // open: cin
  xor xor_1 (\加和输出 , \输入A , \输入B );
  and and_1 (\进位输出 , \输入A , \输入B );

  // Notes on the sheet:
  //   半加器
endmodule

module Full_Adder (
  input  \进位输入 ,
  input  \输入A ,
  input  \输入B ,
  input  in_4,
  input  in_5,
  input  in_6,
  input  in_7,
  input  in_8,
  input  in_9,
  output \加和输出 ,
  output \进位输出 ,
  output out_12,
  output out_13,
  output out_14,
  output out_15
);

  wire adder_1_cout, adder_1_out, adder_3_cout, and_1_out, and_2_out, xor_1_out;

  xor xor_1 (xor_1_out, \输入A , \输入B );
  and and_1 (and_1_out, \输入A , \输入B );
  Adder #(.width(1)) adder_1 (.a(in_5), .b(in_6), .out(adder_1_out), .cout(adder_1_cout));  // open: cin
  Adder #(.width(1)) adder_2 (.a(in_8), .b(in_9), .out(out_14), .cin(in_7), .cout(out_15));
  xor xor_2 (\加和输出 , \进位输入 , xor_1_out);
  and and_2 (and_2_out, \进位输入 , xor_1_out);
  Adder #(.width(1)) adder_3 (.a(in_4), .b(adder_1_out), .out(out_12), .cout(adder_3_cout));  // open: cin
  or or_1 (\进位输出 , and_2_out, and_1_out);
  or or_2 (out_13, adder_3_cout, adder_1_cout);

  // Notes on the sheet:
  //   全加器
endmodule

module _8Bit_Adder (
  input  [7:0] in_1,
  input  [7:0] in_2,
  input  in_3,
  input  [7:0] in_4,
  input  [7:0] in_5,
  input  in_6,
  output out_7,
  output [7:0] out_8,
  output out_9,
  output [7:0] out_10
);

  wire adder_2_cout, adder_3_cout, adder_5_cout, adder_6_cout, adder_7_cout, adder_8_cout, adder_9_cout;

  Adder #(.width(1)) adder_1 (.a(in_2[7]), .b(in_1[7]), .out(out_8[7]), .cin(adder_2_cout), .cout(out_7));
  Adder #(.width(1)) adder_2 (.a(in_2[6]), .b(in_1[6]), .out(out_8[6]), .cin(adder_3_cout), .cout(adder_2_cout));
  Adder #(.width(1)) adder_3 (.a(in_2[5]), .b(in_1[5]), .out(out_8[5]), .cin(adder_5_cout), .cout(adder_3_cout));
  Adder adder_4 (.a(in_5), .b(in_4), .out(out_10), .cin(in_6), .cout(out_9));
  Adder #(.width(1)) adder_5 (.a(in_2[4]), .b(in_1[4]), .out(out_8[4]), .cin(adder_6_cout), .cout(adder_5_cout));
  Adder #(.width(1)) adder_6 (.a(in_2[3]), .b(in_1[3]), .out(out_8[3]), .cin(adder_7_cout), .cout(adder_6_cout));
  Adder #(.width(1)) adder_7 (.a(in_2[2]), .b(in_1[2]), .out(out_8[2]), .cin(adder_8_cout), .cout(adder_7_cout));
  Adder #(.width(1)) adder_8 (.a(in_2[1]), .b(in_1[1]), .out(out_8[1]), .cin(adder_9_cout), .cout(adder_8_cout));
  Adder #(.width(1)) adder_9 (.a(in_2[0]), .b(in_1[0]), .out(out_8[0]), .cin(in_3), .cout(adder_9_cout));

  // Other names for the same wires on the sheet: B0 = in_1[0]; B1 = in_1[1]; B2 = in_1[2]; B3 = in_1[3]; B4 = in_1[4];
  //   B5 = in_1[5]; B6 = in_1[6]; B7 = in_1[7]; A0 = in_2[0]; A1 = in_2[1]; A2 = in_2[2]; A3 = in_2[3]; A4 = in_2[4];
  //   A5 = in_2[5]; A6 = in_2[6]; A7 = in_2[7]

  // Notes on the sheet:
  //   8位二进制加法器
endmodule

module _16Bit_Adder (
  input  [15:0] in_1,
  input  [15:0] in_2,
  input  in_3,
  input  [15:0] in_4,
  input  [15:0] in_5,
  input  in_6,
  output out_7,
  output [15:0] out_8,
  output out_9,
  output [15:0] out_10
);

  wire adder_3_cout;

  Adder adder_1 (.a(in_2[15:8]), .b(in_1[15:8]), .out(out_8[15:8]), .cin(adder_3_cout), .cout(out_7));
  Adder #(.width(16)) adder_2 (.a(in_5), .b(in_4), .out(out_10), .cin(in_6), .cout(out_9));
  Adder adder_3 (.a(in_2[7:0]), .b(in_1[7:0]), .out(out_8[7:0]), .cin(in_3), .cout(adder_3_cout));

  // Notes on the sheet:
  //   16位二进制加法器
endmodule
