// Logisim project 13_lib.circ as structural Verilog: 2 circuits, main circuit 01_Complement
module _01_Complement (
  input  [7:0] \输入 ,
  input  \取反 ,
  output [7:0] out_3
);

  xor xor_1 (out_3[7], \取反 , \输入 [7]);
  xor xor_2 (out_3[6], \取反 , \输入 [6]);
  xor xor_3 (out_3[5], \取反 , \输入 [5]);
  xor xor_4 (out_3[4], \取反 , \输入 [4]);
  xor xor_5 (out_3[3], \取反 , \输入 [3]);
  xor xor_6 (out_3[2], \取反 , \输入 [2]);
  xor xor_7 (out_3[1], \取反 , \输入 [1]);
  xor xor_8 (out_3[0], \取反 , \输入 [0]);

  // Notes on the sheet:
  //   求补器
endmodule

module _02 (
  input  [7:0] \被减数 ,
  input  [7:0] \减数 ,
  input  \加法_减法 ,
  output \溢出 ,
  output [7:0] \输出 
);

  wire adder_1_cout;
  wire [7:0] n01_complement_1_out_3;

  _01_Complement u_01_complement_1 (.\取反 (\加法_减法 ), .\输入 (\减数 ), .out_3(n01_complement_1_out_3));
  xor xor_1 (\溢出 , adder_1_cout, \加法_减法 );
  Adder adder_1 (.a(n01_complement_1_out_3), .b(\被减数 ), .out(\输出 ), .cin(\加法_减法 ), .cout(adder_1_cout));

  // Notes on the sheet:
  //   如果减数小于被减数，这是加法器的CO输出为1。这表示减法的最后一步要减去 1 0000 0000
  //   减法使结果加1
endmodule
