// Logisim project 14_lib.circ as structural Verilog: 9 circuits, main circuit 01_feedback
module _01_feedback (
  input  in_1,
  input  in_2,
  output out_3
);

  wire nor_1_out;

  nor nor_1 (nor_1_out, out_3, in_1);
  nor nor_2 (out_3, nor_1_out, in_2);

  // Notes on the sheet:
  //   反馈
endmodule

module _02_RS (
  input  R,
  input  S,
  input  in_3,
  input  in_4,
  output Q,
  output Q_2,
  output out_7,
  output out_8
);

  nor nor_1 (Q, R, Q_2);
  nor nor_2 (Q_2, Q, S);
  S_R_Flip_Flop #(.trigger("high")) s_r_ff_1 (
    .S(in_3), .clk(1'b1), .R(in_4), .Q(out_7), .Qn(out_8));  // open: preset, reset, en

  // Notes on the sheet:
  //   R-S触发器
endmodule

module _03_D (
  input  Clk,
  input  D,
  input  in_3,
  input  in_4,
  output Q,
  output Q_2,
  output out_7,
  output out_8
);

  wire and_1_out, and_2_out, not_1_out;

  not not_1 (not_1_out, D);
  and and_1 (and_1_out, not_1_out, Clk);
  and and_2 (and_2_out, Clk, D);
  D_Flip_Flop #(.trigger("high")) d_ff_1 (.clk(in_3), .D(in_4), .Q(out_7), .Qn(out_8));  // open: preset, en, reset
  nor nor_1 (Q, and_1_out, Q_2);
  nor nor_2 (Q_2, Q, and_2_out);

  // Notes on the sheet:
  //   电平触发的D型触发器
endmodule

module _04_8Bit_D (
  input  in_1,
  input  [7:0] \输入 ,
  input  [7:0] in_3,
  input  in_4,
  output [7:0] \输出 ,
  output [7:0] out_6
);

  D_Flip_Flop #(.trigger("high")) d_ff_1 (.clk(in_1), .D(\输入 [7]), .Q(\输出 [7]));  // open: Qn, preset, en, reset
  D_Flip_Flop #(.trigger("high")) d_ff_2 (.clk(in_1), .D(\输入 [6]), .Q(\输出 [6]));  // open: Qn, preset, en, reset
  D_Flip_Flop #(.trigger("high")) d_ff_3 (.clk(in_1), .D(\输入 [5]), .Q(\输出 [5]));  // open: Qn, preset, en, reset
  Register #(.trigger("high")) register_1 (.D(in_3), .Q(out_6), .clk(in_4));  // open: en, clr
  D_Flip_Flop #(.trigger("high")) d_ff_4 (.clk(in_1), .D(\输入 [4]), .Q(\输出 [4]));  // open: Qn, preset, en, reset
  D_Flip_Flop #(.trigger("high")) d_ff_5 (.clk(in_1), .D(\输入 [3]), .Q(\输出 [3]));  // open: Qn, preset, en, reset
  D_Flip_Flop #(.trigger("high")) d_ff_6 (.clk(in_1), .D(\输入 [2]), .Q(\输出 [2]));  // open: Qn, preset, en, reset
  D_Flip_Flop #(.trigger("high")) d_ff_7 (.clk(in_1), .D(\输入 [0]), .Q(\输出 [0]));  // open: Qn, preset, en, reset
  D_Flip_Flop #(.trigger("high")) d_ff_8 (.clk(in_1), .D(\输入 [1]), .Q(\输出 [1]));  // open: Qn, preset, en, reset

  // Notes on the sheet:
  //   8位锁存器
endmodule

module _05_2_1 (
  input  A,
  input  \选择端 ,
  input  B,
  input  in_4,
  input  in_5,
  input  in_6,
  output out_7,
  output out_8
);

  wire and_1_out, and_2_out, not_1_out;

  not not_1 (not_1_out, \选择端 );
  and and_1 (and_1_out, A, \选择端 );
  and and_2 (and_2_out, B, not_1_out);
  Multiplexer #(.enable("false")) multiplexer_1 (.in0(in_4), .in1(in_5), .out(out_8), .sel(in_6));
  or or_1 (out_7, and_1_out, and_2_out);

  // Notes on the sheet:
  //   2-1选择器
endmodule

module _06_8Bit_Adder (
  input  [7:0] in_1,
  input  \相加 ,
  input  \清零 ,
  output [7:0] out_4
);

  wire [7:0] adder_1_out;

  Adder adder_1 (.a(out_4), .b(in_1), .out(adder_1_out));  // open: cin, cout
  Register #(.trigger("high")) register_1 (.D(adder_1_out), .Q(out_4), .clk(\相加 ), .clr(\清零 ));  // open: en

  // Notes on the sheet:
  //   8位加法器改进版
endmodule

module _07_edge (
  input  in_1,
  input  in_2,
  input  in_3,
  input  in_4,
  input  in_5,
  input  in_6,
  input  in_7,
  input  in_8,
  output Q,
  output Q_2,
  output out_11,
  output out_12,
  output out_13,
  output out_14,
  output out_15,
  output out_16
);

  wire and_1_out, and_2_out, and_3_out, and_4_out, and_5_out, and_6_out, and_7_out, and_8_out, nor_1_out,
       nor_2_out, not_1_out, not_2_out, not_3_out, not_4_out, s_r_ff_2_q, s_r_ff_2_qn;

  not not_1 (not_1_out, in_2);
  not not_2 (not_2_out, in_5);
  not not_3 (not_3_out, in_1);
  not not_4 (not_4_out, in_6);
  D_Flip_Flop d_ff_1 (.clk(in_7), .D(in_8), .Q(out_15), .Qn(out_16));  // open: preset, en, reset
  and and_1 (and_1_out, in_1, not_1_out);
  and and_2 (and_2_out, not_1_out, not_3_out);
  S_R_Flip_Flop #(.trigger("high")) s_r_ff_1 (
    .S(in_3), .clk(1'b1), .R(in_4), .Q(out_11), .Qn(out_12));  // open: preset, reset, en
  and and_3 (and_3_out, in_5, not_4_out);
  and and_4 (and_4_out, not_4_out, not_2_out);
  S_R_Flip_Flop #(.trigger("high")) s_r_ff_2 (
    .S(and_3_out), .clk(1'b1), .R(and_4_out), .Q(s_r_ff_2_q), .Qn(s_r_ff_2_qn));  // open: preset, reset, en
  nor nor_1 (nor_1_out, and_1_out, nor_2_out);
  nor nor_2 (nor_2_out, nor_1_out, and_2_out);
  and and_5 (and_5_out, s_r_ff_2_q, in_6);
  and and_6 (and_6_out, in_6, s_r_ff_2_qn);
  and and_7 (and_7_out, nor_1_out, in_2);
  and and_8 (and_8_out, in_2, nor_2_out);
  S_R_Flip_Flop #(.trigger("high")) s_r_ff_3 (
    .S(and_5_out), .clk(1'b1), .R(and_6_out), .Q(out_13), .Qn(out_14));  // open: preset, reset, en
  nor nor_3 (Q, and_7_out, Q_2);
  nor nor_4 (Q_2, Q, and_8_out);

  // Notes on the sheet:
  //   边沿触发的D型触发器
  //   电平触发RS
endmodule

module _08_frequency (
  input  in_1,
  input  in_2,
  output out_3,
  output out_4,
  output out_5,
  output out_6,
  output [3:0] out_7
);

  wire d_ff_1_qn, d_ff_2_qn, d_ff_3_qn;

  Counter #(.width(4), .max('hf)) counter_1 (.Q(out_7), .clk(in_2));  // open: load, D, count, carry, clr
  not not_1 (out_3, in_1);
  D_Flip_Flop d_ff_1 (.clk(in_1), .D(d_ff_1_qn), .Q(out_4), .Qn(d_ff_1_qn));  // open: preset, en, reset
  D_Flip_Flop d_ff_2 (.clk(d_ff_1_qn), .D(d_ff_2_qn), .Q(out_5), .Qn(d_ff_2_qn));  // open: preset, en, reset
  D_Flip_Flop d_ff_3 (.clk(d_ff_2_qn), .D(d_ff_3_qn), .Q(out_6), .Qn(d_ff_3_qn));  // open: preset, en, reset

  // Notes on the sheet:
  //   分频器
endmodule

module _09_Counter (
  output [7:0] out_1,
  output [7:0] out_2
);

  wire clock_1_out, clock_2_out, d_ff_1_qn, d_ff_2_qn, d_ff_3_qn, d_ff_4_qn, d_ff_5_qn, d_ff_6_qn, d_ff_7_qn,
       d_ff_8_qn;

  Clock clock_1 (.out(clock_1_out));
  Counter counter_1 (.Q(out_2), .clk(clock_2_out));  // open: load, D, count, carry, clr
  Clock clock_2 (.out(clock_2_out));
  D_Flip_Flop d_ff_1 (.clk(clock_1_out), .D(d_ff_1_qn), .Q(out_1[0]), .Qn(d_ff_1_qn));  // open: preset, en, reset
  D_Flip_Flop d_ff_2 (.clk(d_ff_1_qn), .D(d_ff_2_qn), .Q(out_1[1]), .Qn(d_ff_2_qn));  // open: preset, en, reset
  D_Flip_Flop d_ff_3 (.clk(d_ff_2_qn), .D(d_ff_3_qn), .Q(out_1[2]), .Qn(d_ff_3_qn));  // open: preset, en, reset
  D_Flip_Flop d_ff_4 (.clk(d_ff_3_qn), .D(d_ff_4_qn), .Q(out_1[3]), .Qn(d_ff_4_qn));  // open: preset, en, reset
  D_Flip_Flop d_ff_5 (.clk(d_ff_4_qn), .D(d_ff_5_qn), .Q(out_1[4]), .Qn(d_ff_5_qn));  // open: preset, en, reset
  D_Flip_Flop d_ff_6 (.clk(d_ff_5_qn), .D(d_ff_6_qn), .Q(out_1[5]), .Qn(d_ff_6_qn));  // open: preset, en, reset
  D_Flip_Flop d_ff_7 (.clk(d_ff_6_qn), .D(d_ff_7_qn), .Q(out_1[6]), .Qn(d_ff_7_qn));  // open: preset, en, reset
  D_Flip_Flop d_ff_8 (.clk(d_ff_7_qn), .D(d_ff_8_qn), .Q(out_1[7]), .Qn(d_ff_8_qn));  // open: preset, en, reset
endmodule
