// Logisim project 16_lib.circ as structural Verilog: 5 circuits, main circuit 01_8位锁存器
module \_01_8位锁存器  (
  input  \写操作端 ,
  input  [7:0] \输入端 ,
  input  [7:0] in_3,
  input  in_4,
  output [7:0] \输出端 ,
  output [7:0] out_6
);

  D_Flip_Flop #(.trigger("high")) d_ff_1 (.clk(\写操作端 ), .D(\输入端 [7]), .Q(\输出端 [7]));  // open: Qn, preset, en, reset
  D_Flip_Flop #(.trigger("high")) d_ff_2 (.clk(\写操作端 ), .D(\输入端 [6]), .Q(\输出端 [6]));  // open: Qn, preset, en, reset
  D_Flip_Flop #(.trigger("high")) d_ff_3 (.clk(\写操作端 ), .D(\输入端 [5]), .Q(\输出端 [5]));  // open: Qn, preset, en, reset
  Register #(.trigger("high")) register_1 (.D(in_3), .Q(out_6), .clk(in_4));  // open: en, clr
  D_Flip_Flop #(.trigger("high")) d_ff_4 (.clk(\写操作端 ), .D(\输入端 [4]), .Q(\输出端 [4]));  // open: Qn, preset, en, reset
  D_Flip_Flop #(.trigger("high")) d_ff_5 (.clk(\写操作端 ), .D(\输入端 [3]), .Q(\输出端 [3]));  // open: Qn, preset, en, reset
  D_Flip_Flop #(.trigger("high")) d_ff_6 (.clk(\写操作端 ), .D(\输入端 [2]), .Q(\输出端 [2]));  // open: Qn, preset, en, reset
  D_Flip_Flop #(.trigger("high")) d_ff_7 (.clk(\写操作端 ), .D(\输入端 [1]), .Q(\输出端 [1]));  // open: Qn, preset, en, reset
  D_Flip_Flop #(.trigger("high")) d_ff_8 (.clk(\写操作端 ), .D(\输入端 [0]), .Q(\输出端 [0]));  // open: Qn, preset, en, reset

  // Notes on the sheet:
  //   8位锁存器
endmodule

module _02_RAM_8x1 (
  input  [2:0] \地址 ,
  input  \写操作端 ,
  input  \数据输入 ,
  input  [2:0] in_4,
  input  in_5,
  input  in_6,
  output \数据输出 ,
  output out_8
);

  wire d_ff_1_q, d_ff_2_q, d_ff_3_q, d_ff_4_q, d_ff_5_q, d_ff_6_q, d_ff_7_q, d_ff_8_q, demultiplexer_1_out0,
       demultiplexer_1_out1, demultiplexer_1_out2, demultiplexer_1_out3, demultiplexer_1_out4,
       demultiplexer_1_out5, demultiplexer_1_out6, demultiplexer_1_out7;

  D_Flip_Flop d_ff_1 (.clk(demultiplexer_1_out7), .D(\数据输入 ), .Q(d_ff_1_q));  // open: Qn, preset, en, reset
  D_Flip_Flop d_ff_2 (.clk(demultiplexer_1_out6), .D(\数据输入 ), .Q(d_ff_2_q));  // open: Qn, preset, en, reset
  RAM #(.addrWidth(3), .dataWidth(1), .bus("separate")) ram_1 (
    .addr(in_4), .din(in_5), .data(out_8), .clk(in_6));  // open: str, sel, ld, clr
  Demultiplexer #(.select(3), .enable("false")) demultiplexer_1 (
    .out0(demultiplexer_1_out0), .out1(demultiplexer_1_out1), .out2(demultiplexer_1_out2),
    .out3(demultiplexer_1_out3), .out4(demultiplexer_1_out4), .out5(demultiplexer_1_out5),
    .out6(demultiplexer_1_out6), .out7(demultiplexer_1_out7), .in(\写操作端 ), .sel(\地址 ));
  D_Flip_Flop d_ff_3 (.clk(demultiplexer_1_out5), .D(\数据输入 ), .Q(d_ff_3_q));  // open: Qn, preset, en, reset
  Multiplexer #(.select(3), .enable("false")) multiplexer_1 (
    .in0(d_ff_8_q), .in1(d_ff_7_q), .in2(d_ff_6_q), .in3(d_ff_5_q), .in4(d_ff_4_q), .in5(d_ff_3_q),
    .in6(d_ff_2_q), .in7(d_ff_1_q), .out(\数据输出 ), .sel(\地址 ));
  D_Flip_Flop d_ff_4 (.clk(demultiplexer_1_out4), .D(\数据输入 ), .Q(d_ff_4_q));  // open: Qn, preset, en, reset
  D_Flip_Flop d_ff_5 (.clk(demultiplexer_1_out3), .D(\数据输入 ), .Q(d_ff_5_q));  // open: Qn, preset, en, reset
  D_Flip_Flop d_ff_6 (.clk(demultiplexer_1_out2), .D(\数据输入 ), .Q(d_ff_6_q));  // open: Qn, preset, en, reset
  D_Flip_Flop d_ff_7 (.clk(demultiplexer_1_out1), .D(\数据输入 ), .Q(d_ff_7_q));  // open: Qn, preset, en, reset
  D_Flip_Flop d_ff_8 (.clk(demultiplexer_1_out0), .D(\数据输入 ), .Q(d_ff_8_q));  // open: Qn, preset, en, reset

  // Notes on the sheet:
  //   随机访问存储器 8x1 RAM
endmodule

module _03_RAM_8x2 (
  input  [2:0] \地址 ,
  input  [1:0] \数据输入 ,
  input  \写操作端 ,
  input  [2:0] in_4,
  input  [1:0] in_5,
  input  in_6,
  output [1:0] \数据输出 ,
  output [1:0] out_8
);

  RAM #(.addrWidth(3), .dataWidth(2), .bus("separate")) ram_1 (
    .addr(in_4), .din(in_5), .data(out_8), .clk(in_6));  // open: str, sel, ld, clr
  RAM #(.addrWidth(3), .dataWidth(1), .bus("separate")) ram_2 (
    .addr(\地址 ), .din(\数据输入 [0]), .data(\数据输出 [0]), .clk(\写操作端 ));  // open: str, sel, ld, clr
  RAM #(.addrWidth(3), .dataWidth(1), .bus("separate")) ram_3 (
    .addr(\地址 ), .din(\数据输入 [1]), .data(\数据输出 [1]), .clk(\写操作端 ));  // open: str, sel, ld, clr

  // Notes on the sheet:
  //   随机访问存储器 8x2 RAM
endmodule

module _04_Ram_16x1 (
  input  [3:0] \地址 ,
  input  \写入控制 ,
  input  \数据输入 ,
  input  [3:0] in_4,
  input  in_5,
  input  in_6,
  output out_7,
  output out_8
);

  wire demultiplexer_1_out0, demultiplexer_1_out1, ram_1_data, ram_3_data;

  Demultiplexer #(.enable("false")) demultiplexer_1 (
    .out0(demultiplexer_1_out0), .out1(demultiplexer_1_out1), .in(\数据输入 ), .sel(\地址 [3]));
  RAM #(.addrWidth(3), .dataWidth(1), .bus("separate")) ram_1 (
    .addr(\地址 [2:0]), .din(demultiplexer_1_out0), .data(ram_1_data), .clk(\写入控制 ));  // open: str, sel, ld, clr
  Multiplexer #(.enable("false")) multiplexer_1 (.in0(ram_1_data), .in1(ram_3_data), .out(out_7), .sel(\地址 [3]));
  RAM #(.addrWidth(4), .dataWidth(1), .bus("separate")) ram_2 (
    .addr(in_4), .din(in_5), .data(out_8), .clk(in_6));  // open: str, sel, ld, clr
  LED \u_选择指示灯  ();  // open: in
  RAM #(.addrWidth(3), .dataWidth(1), .bus("separate")) ram_3 (
    .addr(\地址 [2:0]), .din(demultiplexer_1_out1), .data(ram_3_data), .clk(\写入控制 ));  // open: str, sel, ld, clr

  // Notes on the sheet:
  //   随机访问存储器 16x1 RAM
endmodule

module _05_RAM_16x2 (
  input  [3:0] \地址 ,
  input  [1:0] \数据输入 ,
  input  in_3,
  input  [3:0] in_4,
  input  [1:0] in_5,
  input  in_6,
  output [1:0] \数据输出 ,
  output [1:0] out_8
);

  RAM #(.addrWidth(4), .dataWidth(2), .bus("separate")) ram_1 (
    .addr(in_4), .din(in_5), .data(out_8), .clk(in_6));  // open: str, sel, ld, clr
  RAM #(.addrWidth(4), .dataWidth(1), .bus("separate")) ram_2 (
    .addr(\地址 ), .din(\数据输入 [0]), .data(\数据输出 [0]), .clk(in_3));  // open: str, sel, ld, clr
  RAM #(.addrWidth(4), .dataWidth(1), .bus("separate")) ram_3 (
    .addr(\地址 ), .din(\数据输入 [1]), .data(\数据输出 [1]), .clk(in_3));  // open: str, sel, ld, clr

  // Notes on the sheet:
  //   随机访问存储器 16x2 RAM
endmodule
