// Logisim project 17_lib.circ as structural Verilog: 7 circuits, main circuit 01
module _01 (
  input  [7:0] \开关 ,
  input  \相加 ,
  input  \清零 ,
  output [7:0] \输出 
);

  wire [7:0] adder_1_out;

  Adder adder_1 (.a(\输出 ), .b(\开关 ), .out(adder_1_out));  // open: cin, cout
  Register register_1 (.D(adder_1_out), .Q(\输出 ), .clk(\相加 ), .clr(\清零 ));  // open: en
endmodule

module _02 (
  input  \控制开关 ,
  input  [7:0] \数据 ,
  input  [15:0] \地址 ,
  input  in_4,
  input  \清零 ,
  output [7:0] out_6
);

  wire \振荡器_out ;
  wire [7:0] ram_1_data, register_1_q;
  wire [15:0] multiplexer_1_out, \计数器_q ;

  Clock \u_振荡器  (.out(\振荡器_out ));
  Multiplexer #(.width(16), .enable("false")) multiplexer_1 (
    .in0(\地址 ), .in1(\计数器_q ), .out(multiplexer_1_out), .sel(\控制开关 ));
  Counter #(.width(16), .max('hffff)) \u_计数器  (
    .Q(\计数器_q ), .clk(\振荡器_out ), .clr(\清零 ));  // open: load, D, count, carry
  RAM #(.addrWidth(16), .bus("separate")) ram_1 (
    .addr(multiplexer_1_out), .din(\数据 ), .data(ram_1_data), .clk(in_4));  // open: str, sel, ld, clr
  Adder adder_1 (.a(ram_1_data), .b(register_1_q), .out(out_6));  // open: cin, cout
  Register register_1 (.D(out_6), .Q(register_1_q), .clk(\振荡器_out ), .clr(\清零 ));  // open: en

  // Notes on the sheet:
  //   把 RAM 阵列和累加器连接起来
endmodule

module _03 (
  input  \控制开关 ,
  input  [7:0] \数据 ,
  input  [15:0] \地址 ,
  input  in_4,
  input  \清零 ,
  output [7:0] out_6
);

  wire \振荡器_out ;
  wire [7:0] multiplexer_2_out, ram_1_data, register_1_q;
  wire [15:0] multiplexer_1_out, \计数器_q ;

  Clock \u_振荡器  (.out(\振荡器_out ));
  Multiplexer #(.width(16), .enable("false")) multiplexer_1 (
    .in0(\地址 ), .in1(\计数器_q ), .out(multiplexer_1_out), .sel(\控制开关 ));
  Counter #(.width(16), .max('hffff)) \u_计数器  (
    .Q(\计数器_q ), .clk(\振荡器_out ), .clr(\清零 ));  // open: load, D, count, carry
  Multiplexer #(.width(8), .enable("false")) multiplexer_2 (
    .in0(\数据 ), .in1(register_1_q), .out(multiplexer_2_out), .sel(\控制开关 ));
  RAM #(.addrWidth(16), .bus("separate")) ram_1 (
    .addr(multiplexer_1_out), .din(multiplexer_2_out), .data(ram_1_data), .clk(in_4));  // open: str, sel, ld, clr
  Adder adder_1 (.a(ram_1_data), .b(register_1_q), .out(out_6));  // open: cin, cout
  Register register_1 (.D(out_6), .Q(register_1_q), .clk(\振荡器_out ), .clr(\清零 ));  // open: en

  // Notes on the sheet:
  //   把运算结果存回到 RAM 阵列中去
endmodule

module _04 (
  output [7:0] \代码 ,
  output [7:0] \数据 
);

  wire [15:0] counter_1_q;

  Counter #(.width(16), .max('hffff)) counter_1 (.Q(counter_1_q));  // open: load, D, count, carry, clk, clr
  RAM #(.addrWidth(16), .bus("separate")) ram_1 (.addr(counter_1_q), .data(\代码 ));  // open: din, str, sel, clk, ld, clr
  RAM #(.addrWidth(16), .bus("separate")) ram_2 (.addr(counter_1_q), .data(\数据 ));  // open: din, str, sel, clk, ld, clr

  // Notes on the sheet:
  //   操作码
endmodule

module _05 (
  input  \Load指令_10h ,
  output [7:0] \代码 
);

  wire [7:0] adder_1_out, multiplexer_1_out, ram_2_data, register_1_q;
  wire [15:0] counter_1_q;

  Counter #(.width(16), .max('hffff)) counter_1 (.Q(counter_1_q));  // open: load, D, count, carry, clk, clr
  RAM #(.addrWidth(16), .bus("separate")) ram_1 (.addr(counter_1_q), .data(\代码 ));  // open: din, str, sel, clk, ld, clr
  RAM #(.addrWidth(16), .bus("separate")) ram_2 (
    .addr(counter_1_q), .din(register_1_q), .data(ram_2_data));  // open: str, sel, clk, ld, clr
  Multiplexer #(.width(8), .enable("false")) multiplexer_1 (
    .in0(ram_2_data), .in1(adder_1_out), .out(multiplexer_1_out), .sel(\Load指令_10h ));
  Adder adder_1 (.a(register_1_q), .b(ram_2_data), .out(adder_1_out));  // open: cin, cout
  Register register_1 (.D(multiplexer_1_out), .Q(register_1_q));  // open: en, clk, clr

  // Notes on the sheet:
  //   Save指令_11h
  //   Add指令_20h
endmodule

module _06 (
  input  \Load指令_10h ,
  output [7:0] \代码 
);

  wire undriven;
  wire [7:0] adder_1_out, controlled_inverter_1_out, multiplexer_1_out, ram_2_data, register_1_q;
  wire [15:0] counter_1_q;

  Counter #(.width(16), .max('hffff)) counter_1 (.Q(counter_1_q));  // open: load, D, count, carry, clk, clr
  RAM #(.addrWidth(16), .bus("separate")) ram_1 (.addr(counter_1_q), .data(\代码 ));  // open: din, str, sel, clk, ld, clr
  RAM #(.addrWidth(16), .bus("separate")) ram_2 (
    .addr(counter_1_q), .din(register_1_q), .data(ram_2_data));  // open: str, sel, clk, ld, clr
  Multiplexer #(.width(8), .enable("false")) multiplexer_1 (
    .in0(ram_2_data), .in1(adder_1_out), .out(multiplexer_1_out), .sel(\Load指令_10h ));
  Register register_1 (.D(multiplexer_1_out), .Q(register_1_q));  // open: en, clk, clr
  assign controlled_inverter_1_out = undriven ? ~ram_2_data : 8'bz;  // Controlled_Inverter controlled_inverter_1
  Adder adder_1 (.a(register_1_q), .b(controlled_inverter_1_out), .out(adder_1_out));  // open: cin, cout

  // Notes on the sheet:
  //   Save指令_11h
  //   Add指令_20h
  //   反向器用于减法
endmodule

module _07 (
);

  wire [7:0] ram_1_data, register_1_q, register_2_q, register_3_q;

  RAM #(.addrWidth(16), .bus("separate")) ram_1 (.data(ram_1_data));  // open: addr, din, str, sel, clk, ld, clr
  Register register_1 (.D(ram_1_data), .Q(register_1_q));  // open: en, clk, clr
  Register register_2 (.D(ram_1_data), .Q(register_2_q));  // open: en, clk, clr
  Register register_3 (.D(ram_1_data), .Q(register_3_q));  // open: en, clk, clr
  RAM #(.addrWidth(16), .bus("separate")) ram_2 (.addr({register_3_q, register_2_q}));  // open: din, data, str, sel, clk, ld, clr
endmodule
